// Logisim project Aula_06-08.circ as structural Verilog: 2 circuits, main circuit main
module main (
  input  G,
  input  H,
  input  Vem_1,
  output S,
  output Vai_1
);

  wire and_1_out, and_2_out, or_1_out, xor_1_out;

  xor xor_1 (xor_1_out, G, H);
  or or_1 (or_1_out, H, Vem_1);
  xor xor_2 (S, xor_1_out, Vem_1);
  and and_1 (and_1_out, or_1_out, G);
  or or_2 (Vai_1, and_1_out, and_2_out);
  and and_2 (and_2_out, H, Vem_1);
endmodule

module Add_1 (
  input  in_1,
  input  in_2,
  input  Vem_1,
  output Vai_1,
  output out_5,
  output out_6,
  output out_7
);

  wire main_3_vai_1, main_4_vai_1, main_5_vai_1;
  wire [3:0] main_5_s, undriven, undriven_2;

  main main_1 (.G(in_1), .H(in_2), .Vem_1(Vem_1), .S(out_5), .Vai_1(Vai_1));
  main main_2 (.G(undriven_2[3]), .H(undriven[3]), .Vem_1(main_3_vai_1), .S(main_5_s[3]), .Vai_1(out_6));
  main main_3 (.G(undriven_2[2]), .H(undriven[2]), .Vem_1(main_4_vai_1), .S(main_5_s[2]), .Vai_1(main_3_vai_1));
  main main_4 (.G(undriven_2[1]), .H(undriven[1]), .Vem_1(main_5_vai_1), .S(main_5_s[1]), .Vai_1(main_4_vai_1));
  main main_5 (.G(undriven_2[0]), .H(undriven[0]), .Vem_1(out_7), .S(main_5_s[0]), .Vai_1(main_5_vai_1));
endmodule
